# Fritzing sketch Ambient sensor wire sketch (saved by Fritzing 0.9.9b)
breadboards: 1

parts:
  U2 = NodeMCU V3.0
  U3 = POT [package=pot_mammoth]
  S4 = Toggle Switch [package=THT]
  R1 = Resistor [tolerance=±5% power=0.25 resistance=220 package=THT]
  S5 = Pushbutton [package="[THT]"]
  R2 = Resistor [tolerance=±5% power=0.25 resistance=220 package=THT]
  Mod2 = KY-012 Active Buzzer Module [package="Breakout board"]
  Q1 = TRANSISTOR_NPN [package=to-92-ammo]
  R3 = Resistor [tolerance=±5% power=0.25 resistance=100 package=THT]
  DHT1 = DHT11 Humitidy and Temperature Sensor
  R4 = Resistor [tolerance=±5% power=0.25 resistance=10k package=THT]
  Part1 = HC-SR501 Body Sensor Module
  LCD1 = LCD screen
  LCM1602_IIC1 = LCM1602 IIC [part_number="LCM1602 IIC" chip_label="LCM1602 IIC" package="DIP (Dual Inline) [THT]"]

nets:
  N1: U2.D0, S4.COM
  N2: U2.D1, LCM1602_IIC1.SCL
  N3: U2.D2, LCM1602_IIC1.SDA
  3V3: U2.3V3, U3.E, S4.L2, S5.Pin_3, S5.Pin_4, DHT1.VDD, R4.Pin_0
  GND: U2.GND#6, U2.GND#13, U2.GND#16, U2.GND#33, U3.S, R1.Pin_0, R2.Pin_0, Q1.C, DHT1.GND, Part1.GND, LCM1602_IIC1.GND
  N4: U2.D5, R3.Pin_1
  N5: U2.D6, DHT1.DATA, R4.Pin_1
  N6: U2.D7, Part1.OUT
  N7: U2.D8, S5.Pin_1, S5.Pin_2, R2.Pin_1
  VCC: U2.Vin, Mod2.S, Part1.VCC, LCM1602_IIC1.VCC
  N8: U2.A0, U3.A
  N9: S4.L1, R1.Pin_1
  N10: Mod2.-, Q1.E
  N11: Q1.B, R3.Pin_0
  VSS: LCD1.VSS, LCM1602_IIC1.VSS
  VDD: LCD1.VDD, LCM1602_IIC1.VDD
  N12: LCD1.V0, LCM1602_IIC1.V0
  N13: LCD1.RS, LCM1602_IIC1.RS
  N14: LCD1.R/W, LCM1602_IIC1.RW
  N15: LCD1.E, LCM1602_IIC1.E
  N16: LCD1.DB0, LCM1602_IIC1.D0
  N17: LCD1.DB1, LCM1602_IIC1.D1
  N18: LCD1.DB2, LCM1602_IIC1.D2
  N19: LCD1.DB3, LCM1602_IIC1.D3
  N20: LCD1.DB4, LCM1602_IIC1.D4
  N21: LCD1.DB5, LCM1602_IIC1.D5
  N22: LCD1.DB6, LCM1602_IIC1.D6
  N23: LCD1.DB7, LCM1602_IIC1.D7
  N24: LCD1.LED+, LCM1602_IIC1.A
  N25: LCD1.LED-, LCM1602_IIC1.K

custom parts:
  NodeMCU V3.0: ESP8266 based NodeMCU
  KY-012 Active Buzzer Module: Active Piezoelectric Buzzer Module KY-012, it produces single-tone sound when signal is high. (Special thanks to vanepp for fixing the PCB holes and other errors)
  DHT11 Humitidy and Temperature Sensor: DHT11 Humidity and Temperature Sensor
  HC-SR501 Body Sensor Module: Pyroelectric Infrared PIR Motion Sensor Detector Module
  LCM1602 IIC: I2C-Module to use a 1602 or 2004 LCD on with the wire.h libory Serial LCD Modul
