# Fritzing sketch checkInOutModule Wiring Sketch complete (saved by Fritzing 0.9.9b)
breadboards: 1

parts:
  U1 = NodeMCU V3.0
  OLED_I2C1 = OLED 128x64 I2C Monochrome Display
  S2 = Pushbutton [package="[THT]"]
  R1 = Resistor [tolerance=±5% power=0.25 resistance=220 package=THT]
  U2 = POT [package=pot_mammoth]
  S3 = Toggle Switch [package=THT]
  R2 = Resistor [tolerance=±5% power=0.25 resistance=220 package=THT]
  S4 = Pushbutton [package="[THT]"]
  R3 = Resistor [tolerance=±5% power=0.25 resistance=220 package=THT]
  Part1 = HX711 Weighing Sensor Module
  Load_Cell1 = Load Cell - Red/white/black/green

nets:
  N1: U1.D0, S3.COM
  N2: U1.D1, OLED_I2C1.SCK
  N3: U1.D2, OLED_I2C1.SDA
  3V3: U1.3V3, OLED_I2C1.VDD, U2.E, S3.L2
  GND: U1.GND#6, U1.GND#13, U1.GND#16, U1.GND#33, OLED_I2C1.GND, S2.Pin_3, S2.Pin_4, R1.Pin_1, U2.S, R2.Pin_0, S4.Pin_3, S4.Pin_4, R3.Pin_0, Part1.GND
  N4: U1.D5, Part1.DO/RX
  N5: U1.D6, Part1.CK/TX
  N6: U1.D7, S2.Pin_1, S2.Pin_2, R1.Pin_0
  N7: U1.D8, S4.Pin_1, S4.Pin_2, R3.Pin_1
  VIN: U1.Vin, Part1.VCC
  N8: U1.A0, U2.A
  N9: S3.L1, R2.Pin_1
  N10: Part1.E+, Load_Cell1.wire1
  N11: Part1.E-, Load_Cell1.wire3
  N12: Part1.A+, Load_Cell1.wire2
  N13: Part1.A-, Load_Cell1.wire4

custom parts:
  NodeMCU V3.0: ESP8266 based NodeMCU
  Load Cell - Red/white/black/green: A rectangle load cell/weighting pressure Sensor with four wires - Red, white, black, green. Normally corresponding with E+, E-, A+, A- respectively.
